# Fritzing sketch Pin Diagram (saved by Fritzing 0.9.3b)

parts:
  OBC = XIAO ESP32C3-smd
  Comms = RYLR896 [package=THT]
  Power = DC_DC_XL4016 [package=board_screw]
  7_4V = LIPO-110mAh [package=lipo-110]
  Position_&_Orientation = bn-220- GPS-module
  Sensor = BME280
  Position_&_Orientation_2 = InvenSense MPU6050
  Sensor_2 = Adafruit INA219

nets:
  GND: OBC.Pin_2, OBC.Pin_7, OBC.Pin_21, Comms.pin5, Power.OUT-, Position_&_Orientation.pin_1, Sensor.GND, Position_&_Orientation_2.GND, Sensor_2.GND, Sensor_2.VIN-
  3.3V: OBC.Pin_8, Comms.pin1, Power.OUT+, Position_&_Orientation.pin_4, Sensor.VIN, Position_&_Orientation_2.VCC, Sensor_2.VCC, Sensor_2.VIN+
  N1: OBC.Pin_9, Comms.pin3#2
  N2: OBC.Pin_10, Comms.pin3#3
  N3: OBC.Pin_11, Position_&_Orientation.pin_3
  N4: OBC.Pin_12, Position_&_Orientation.pin_2
  N5: OBC.Pin_13, Sensor.SDA, Position_&_Orientation_2.SDA, Sensor_2.SDA
  N6: OBC.Pin_14, Sensor.SCL, Position_&_Orientation_2.SCL, Sensor_2.SCL
  N7: Power.IN+, 7_4V.+
  N8: Power.IN-, 7_4V.-

custom parts:
  XIAO ESP32C3-smd: Seeed Studio XIAO ESP32C3 adopts new RISC-V architecture, supporting both Wi-Fi and BLE wireless connectivities.
  RYLR896: RYLR896 UART Interface 868/915mhz LORA Transceiver Module
  DC_DC_XL4016: DC-DC Converter step down voltage regulator XL4016 custom sketch.
  bn-220- GPS-module: bn-220l GPS module. Chipset : 8030-KT Receiving Format : GPS,GLONASS,Galileo,BeiDou,QZSS and SBAS
  BME280: Temperature Humidity Barometric presure Sensor
  Adafruit INA219: This breakout board will solve all your power-monitoring problems. Instead of struggling with two multimeters, you can just use the handy INA219B chip on this breakout to both measure both the high side voltage and DC current draw over I2C with 1% precision. Most current-measuring devices such as our current panel meter are only good for low side measuring. That means that unless you want to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
